// Logisim project progetto.circ as structural Verilog: 6 circuits, main circuit main
module main (
  output [4:0] out_1,
  output [4:0] out_2,
  output [4:0] out_3,
  output [4:0] out_4
);

  wire _0_out, _1_out, _2_out, _3_out, _4_out, _5_out, _6_out, _7_out, _8_out, _9_out, button_2_out,
       button_out, clock_1_out, keypad_1_clicked, minus_1_out_2, OK_out, or_1_out;
  wire [1:0] counter_1_q;
  wire [3:0] keypad_1_b0;
  wire [4:0] calcolo_1_out_5, counter_2_q, demultiplexer_1_out0, multiplexer_1_out, negativator_1_out_2,
       register_1_q;
  wire [31:0] decoder_1_out0;

  Button _7 (.out(_7_out));
  Button _8 (.out(_8_out));
  Button _4 (.out(_4_out));
  Button _5 (.out(_5_out));
  Button _1 (.out(_1_out));
  Button _2 (.out(_2_out));
  Button _0 (.out(_0_out));
  Button OK (.out(OK_out));
  Button button (.out(button_out));
  DotMatrix #(.matrixcols(32), .matrixrows(32)) dotmatrix_1 (
    .col0(decoder_1_out0), .col1(decoder_1_out0), .col2(decoder_1_out0), .col3(decoder_1_out0),
    .col4(decoder_1_out0), .col5(decoder_1_out0), .col6(decoder_1_out0), .col7(decoder_1_out0),
    .col8(decoder_1_out0), .col9(decoder_1_out0), .col10(decoder_1_out0), .col11(decoder_1_out0),
    .col12(decoder_1_out0), .col13(decoder_1_out0), .col14(decoder_1_out0));  // open: col15, col16, col17, col18, col19, col20, col21, col22, col23, col24, col25, col26, col27, col28, col29, col30, col31
  Button _9 (.out(_9_out));
  Button _6 (.out(_6_out));
  Button _3 (.out(_3_out));
  Button button_2 (.out(button_2_out));
  or or_1 (or_1_out, OK_out, button_out);
  keypad keypad_1 (
    ._0(_0_out), ._1(_1_out), ._3(_3_out), ._2(_2_out), ._5(_5_out), ._4(_4_out), ._7(_7_out), ._6(_6_out),
    .b2_2(keypad_1_b0[2]), .b1(keypad_1_b0[1]), .b0(keypad_1_b0[0]), ._8(_8_out), ._9(_9_out),
    .b2(keypad_1_b0[3]), .clicked(keypad_1_clicked));
  minus minus_1 (.in_1(button_2_out), .out_2(minus_1_out_2));
  LED meno (.in(minus_1_out_2));
  Counter #(.width(2), .max('h2), .trigger("falling")) counter_1 (
    .Q(counter_1_q), .clk(or_1_out));  // open: load, D, count, carry, clr
  Multiplexer #(.width(5)) multiplexer_1 (
    .in0({1'b0, keypad_1_b0}), .in1(negativator_1_out_2), .out(multiplexer_1_out), .sel(minus_1_out_2));  // open: en
  negativator negativator_1 (.in_1({1'b0, keypad_1_b0}), .out_2(negativator_1_out_2));
  Counter #(.width(5), .max('h1f)) counter_2 (.Q(counter_2_q), .clk(clock_1_out));  // open: load, D, count, carry, clr
  Clock clock_1 (.out(clock_1_out));
  // AND_Gate and_1 has open pins: in5=clock_1_out, out=open
  Decoder #(.select(5)) decoder_1 (
    .out0(decoder_1_out0[0]), .out1(decoder_1_out0[1]), .out2(decoder_1_out0[2]), .out3(decoder_1_out0[3]),
    .out4(decoder_1_out0[4]), .out5(decoder_1_out0[5]), .out6(decoder_1_out0[6]), .out7(decoder_1_out0[7]),
    .out8(decoder_1_out0[8]), .out9(decoder_1_out0[9]), .sel(register_1_q));  // open: out10, out11, out12, out13, out14, out15, out16, out17, out18, out19, out20, out21, out22, out23, out24, out25, out26, out27, out28, out29, out30, out31, en
  memory memory_1 (
    .in_1(multiplexer_1_out), .in_2(keypad_1_clicked), .in_3(OK_out), .in_4(counter_1_q), .out_5(out_1),
    .out_6(out_2), .out_7(out_3), .out_8(out_4));
  Register #(.width(5)) register_1 (.D(demultiplexer_1_out0), .Q(register_1_q));  // open: en, clk, clr
  calcolo calcolo_1 (.c_x_2(out_1), .c_x(out_2), .q(out_3), .out_5(calcolo_1_out_5), .x(counter_2_q));
  Demultiplexer #(.select(5), .width(5)) demultiplexer_1 (
    .out0(demultiplexer_1_out0), .in(calcolo_1_out_5), .sel(counter_2_q));  // open: out1, out2, out3, out4, out5, out6, out7, out8, out9, out10, out11, out12, out13, out14, out15, out16, out17, out18, out19, out20, out21, out22, out23, out24, out25, out26, out27, out28, out29, out30, out31, en
endmodule

module keypad (
  input  _0,
  input  _1,
  input  _3,
  input  _2,
  input  _5,
  input  _4,
  input  _7,
  input  _6,
  input  _9,
  input  _8,
  output clicked,
  output b2,
  output b2_2,
  output b1,
  output b0
);

  or or_1 (b0, _1, _9, _3, _5, _7);
  or or_2 (b1, _3, _2, _7, _6);
  or or_3 (b2_2, _6, _5, _7, _4);
  or or_4 (b2, _9, _8);
  or or_5 (clicked, _0, b0, b1, b2_2, b2);
endmodule

module negativator (
  input  [4:0] in_1,
  output [4:0] out_2
);

  wire [4:0] not_1_out;

  assign not_1_out = ~in_1;  // NOT_Gate not_1, 5 bits wide
  Adder #(.width(5)) adder_1 (.a(not_1_out), .b(5'b00001), .out(out_2));  // open: cin, cout
endmodule

module memory (
  input  [4:0] in_1,
  input  in_2,
  input  in_3,
  input  [1:0] in_4,
  output [4:0] out_5,
  output [4:0] out_6,
  output [4:0] out_7,
  output [4:0] out_8
);

  wire demultiplexer_2_out0, demultiplexer_2_out1, demultiplexer_2_out2, demultiplexer_2_out3;
  wire [4:0] d_ff_1_q, demultiplexer_1_out0, demultiplexer_1_out1, demultiplexer_1_out2, demultiplexer_1_out3;

  D_Flip_Flop #(.trigger("high")) d_ff_1 (.clk(in_2), .D(in_1[0]), .Q(d_ff_1_q[0]));  // open: Qn, preset, en, reset
  D_Flip_Flop #(.trigger("high")) d_ff_2 (.clk(in_2), .D(in_1[1]), .Q(d_ff_1_q[1]));  // open: Qn, preset, en, reset
  D_Flip_Flop #(.trigger("high")) d_ff_3 (.clk(in_2), .D(in_1[2]), .Q(d_ff_1_q[2]));  // open: Qn, preset, en, reset
  D_Flip_Flop #(.trigger("high")) d_ff_4 (.clk(in_2), .D(in_1[3]), .Q(d_ff_1_q[3]));  // open: Qn, preset, en, reset
  D_Flip_Flop #(.trigger("high")) d_ff_5 (.clk(in_2), .D(in_1[4]), .Q(d_ff_1_q[4]));  // open: Qn, preset, en, reset
  Demultiplexer #(.select(2), .width(5)) demultiplexer_1 (
    .out0(demultiplexer_1_out0), .out1(demultiplexer_1_out1), .out2(demultiplexer_1_out2),
    .out3(demultiplexer_1_out3), .in(d_ff_1_q), .sel(in_4));  // open: en
  Demultiplexer #(.select(2)) demultiplexer_2 (
    .out0(demultiplexer_2_out0), .out1(demultiplexer_2_out1), .out2(demultiplexer_2_out2),
    .out3(demultiplexer_2_out3), .in(in_3), .sel(in_4));  // open: en
  Register #(.width(5), .trigger("high")) register_1 (
    .D(demultiplexer_1_out0), .Q(out_5), .clk(demultiplexer_2_out0));  // open: en, clr
  Register #(.width(5), .trigger("high")) register_2 (
    .D(demultiplexer_1_out1), .Q(out_6), .clk(demultiplexer_2_out1));  // open: en, clr
  Register #(.width(5), .trigger("high")) register_3 (
    .D(demultiplexer_1_out2), .Q(out_7), .clk(demultiplexer_2_out2));  // open: en, clr
  Register #(.width(5), .trigger("high")) register_4 (
    .D(demultiplexer_1_out3), .Q(out_8), .clk(demultiplexer_2_out3));  // open: en, clr
endmodule

module minus (
  input  in_1,
  output out_2
);

  wire and_1_out, d_ff_1_qn;

  and and_1 (and_1_out, in_1, d_ff_1_qn);
  D_Flip_Flop #(.trigger("falling")) d_ff_1 (
    .clk(in_1), .D(and_1_out), .Q(out_2), .Qn(d_ff_1_qn));  // open: preset, en, reset
endmodule

module calcolo (
  input  [4:0] c_x_2,
  input  [4:0] c_x,
  input  [4:0] q,
  input  [4:0] x,
  output [4:0] out_5
);

  wire adder_1_cout;
  wire [4:0] adder_1_out, multiplier_1_out, multiplier_2_cout, multiplier_2_out, multiplier_3_out;

  Multiplier #(.width(5)) multiplier_1 (.a(c_x), .b(x), .out(multiplier_1_out));  // open: cin, cout
  Multiplier #(.width(5)) multiplier_2 (
    .a(c_x_2), .b(x), .out(multiplier_2_out), .cout(multiplier_2_cout));  // open: cin
  Multiplier #(.width(5)) multiplier_3 (
    .a(multiplier_2_out), .b(x), .out(multiplier_3_out), .cin(multiplier_2_cout));  // open: cout
  Adder #(.width(5)) adder_1 (
    .a(multiplier_3_out), .b(multiplier_1_out), .out(adder_1_out), .cout(adder_1_cout));  // open: cin
  Adder #(.width(5)) adder_2 (.a(q), .b(adder_1_out), .out(out_5), .cin(adder_1_cout));  // open: cout
endmodule
